// Logisim project MediaAritmetica.circ as structural Verilog
module BOARD_BIG_ASM (
  output out_1
);

  wire button_1_out, CLK, CLR, d_ff_1_q, not_1_out, Write, Write_ASCII;
  wire [6:0] ASCII;
  wire [7:0] counter_1_q;
  wire [23:0] Dir_INPUT, Dir_MEMORY;
  wire [31:0] INPUT, MEMORY_IN, MEMORY_OUT;

  Button button_1 (.out(button_1_out));
  Clock clock_1 (.out(CLK));
  D_Flip_Flop d_ff_1 (.clk(CLK), .D(1'b1), .Q(d_ff_1_q), .reset(button_1_out));  // open: Qn, preset, en
  D_Flip_Flop d_ff_2 (.clk(CLK), .D(d_ff_1_q), .Qn(CLR), .reset(button_1_out));  // open: Q, preset, en
  BIG_ASM big_asm_1 (
    .DATA_INPUT(INPUT), .MEMORY_IN(MEMORY_OUT), .CLK(CLK), .CLR(CLR), .DIR_INPUT(Dir_INPUT),
    .MEMORY_OUT(MEMORY_IN), .DIR_MEMORY(Dir_MEMORY), .Write_OUTPUT(Write), .ASCII(ASCII),
    .Write_ASCII(Write_ASCII), .END(out_1));
  MEMORY memory_1 (.DIR(Dir_MEMORY), .DATA_IN(MEMORY_IN), .WRITE(Write), .CLK(CLK), .CLR(CLR), .DATA_OUT(MEMORY_OUT));
  INPUT input_1 (.DIR(Dir_INPUT), .CLK(CLK), .DATA_OUT(INPUT));
  Counter counter_1 (.load(1'b0), .count(not_1_out), .Q(counter_1_q), .clk(CLK), .clr(CLR));  // open: D, carry
  not not_1 (not_1_out, out_1);
  // Probe on counter_1_q
  TTY #(.rows(32), .cols(60)) tty_1 (.data(ASCII), .clk(CLK), .we(Write_ASCII), .clr(CLR));

  // Other names for the same wires on the sheet: END = out_1

  // Notes on the sheet:
  //   COUNTER
  //   BOARD
endmodule

module INPUT (
  input  [23:0] DIR,
  input  CLK,
  output [31:0] DATA_OUT
);

  RAM #(.addrWidth(24), .dataWidth(32)) ram_1 (.addr(DIR), .data(DATA_OUT), .clk(CLK), .ld(1'b1));  // open: sel, clr
endmodule

module MEMORY (
  input  [23:0] DIR,
  input  [31:0] DATA_IN,
  input  WRITE,
  input  CLK,
  input  CLR,
  output [31:0] DATA_OUT
);

  RAM #(.addrWidth(24), .dataWidth(32), .bus("separate")) ram_1 (
    .addr(DIR), .din(DATA_IN), .data(DATA_OUT), .str(WRITE), .clk(CLK), .clr(CLR));  // open: sel, ld
endmodule

module BIG_ASM (
  input  [31:0] DATA_INPUT,
  input  [31:0] MEMORY_IN,
  input  CLK,
  input  CLR,
  output [23:0] DIR_INPUT,
  output [31:0] MEMORY_OUT,
  output [23:0] DIR_MEMORY,
  output Write_OUTPUT,
  output [6:0] ASCII,
  output Write_ASCII,
  output END
);

  wire CLK_t, comparator_1_eq, end_t, not_1_out, not_2_out;
  wire [6:0] register_1_q;
  wire [31:0] result;

  not not_1 (not_1_out, CLR);
  and and_1 (CLK_t, CLK, not_2_out);
  not not_2 (not_2_out, END);
  SubASM subasm_1 (
    .elemento(DATA_INPUT), .start(not_1_out), .reloj(CLK_t), .in_4(END), .resultado(result), .\end (end_t));
  PRINT_DEC print_dec_1 (
    .num(result), .start(end_t), .CLK(CLK_t), .RST(CLR), .ASCII(ASCII), .END(END));  // open: Write_ASCII
  Register #(.width(7)) register_1 (.D(ASCII), .Q(register_1_q), .clk(CLK_t), .clr(CLR));  // open: en
  Counter #(.width(24), .max('hffffff)) counter_1 (
    .Q(DIR_INPUT), .clk(CLK_t), .clr(CLR));  // open: load, D, count, carry
  Comparator #(.width(7), .mode("unsigned")) comparator_1 (
    .a(register_1_q), .b(ASCII), .eq(comparator_1_eq));  // open: gt, lt
  not not_3 (Write_ASCII, comparator_1_eq);
endmodule

module PRINT_UDEC (
  input  [31:0] num,
  input  start,
  input  CLK,
  input  RST,
  output [6:0] ASCII,
  output Write_ASCII,
  output \end 
);

  wire _0_c, _0_n, demultiplexer_1_out0, demultiplexer_2_out0, demultiplexer_2_out1, demultiplexer_3_out0,
       demultiplexer_3_out1, IDLE_2_q, IDLE_3_q, IDLE_4_q, IDLE_q, Lc, Lc_0, Ln, Ln_0, or_1_out;
  wire [23:0] bit_extender_1_out;
  wire [31:0] c, c___1, c___1_t, divider_1_rem, memory_1_data_out, multiplexer_1_out, multiplexer_2_out,
       multiplexer_3_out, n, n___10, n___10___48;

  Multiplexer #(.width(32), .enable("false")) multiplexer_1 (
    .in0(num), .in1(n___10), .out(multiplexer_1_out), .sel(Lc_0));
  Divider #(.width(32)) divider_1 (.a(n), .b(32'ha), .out(n___10), .rem(divider_1_rem));  // open: upper
  Adder #(.width(32)) adder_1 (.a(divider_1_rem), .b(32'h30), .out(n___10___48));  // open: cin, cout
  or or_1 (or_1_out, demultiplexer_1_out0, \end );
  Register #(.width(32)) u_n (.D(multiplexer_1_out), .en(Ln), .Q(n), .clk(CLK), .clr(RST));
  D_Flip_Flop IDLE (.clk(CLK), .D(or_1_out), .Q(IDLE_q), .preset(RST));  // open: Qn, en, reset
  Demultiplexer #(.enable("false")) demultiplexer_1 (
    .out0(demultiplexer_1_out0), .out1(Ln_0), .in(IDLE_q), .sel(start));
  or or_2 (Write_ASCII, demultiplexer_3_out0, demultiplexer_2_out1);
  Multiplexer #(.width(32), .enable("false")) multiplexer_2 (
    .in0(c___1), .in1(c___1_t), .out(multiplexer_2_out), .sel(Write_ASCII));
  Adder #(.width(32)) adder_2 (.a(c), .b(32'h1), .out(c___1));  // open: cin, cout
  Subtractor #(.width(32)) subtractor_1 (.a(c), .b(32'h1), .out(c___1_t));  // open: bin, bout
  D_Flip_Flop IDLE_2 (.clk(CLK), .D(Ln_0), .Q(IDLE_2_q), .reset(RST));  // open: Qn, preset, en
  Register #(.width(32)) u_c (.D(multiplexer_2_out), .en(Lc), .Q(c), .clk(CLK), .clr(RST));
  or or_3 (Lc_0, IDLE_2_q, demultiplexer_3_out1);
  Multiplexer #(.width(32), .enable("false")) multiplexer_3 (
    .in0(c), .in1(c___1_t), .out(multiplexer_3_out), .sel(Write_ASCII));
  Comparator #(.width(32), .mode("unsigned")) comparator_1 (.a({32{1'b0}}), .b(n), .lt(_0_n));  // open: gt, eq
  Comparator #(.width(32), .mode("unsigned")) comparator_2 (.a({32{1'b0}}), .b(c), .lt(_0_c));  // open: gt, eq
  D_Flip_Flop IDLE_3 (.clk(CLK), .D(Write_ASCII), .Q(IDLE_3_q), .reset(RST));  // open: Qn, preset, en
  Demultiplexer #(.enable("false")) demultiplexer_2 (
    .out0(demultiplexer_2_out0), .out1(demultiplexer_2_out1), .in(IDLE_3_q), .sel(_0_c));
  Bit_Extender #(.in_width(32), .out_width(24)) bit_extender_1 (.in(multiplexer_3_out), .out(bit_extender_1_out));
  D_Flip_Flop IDLE_4 (.clk(CLK), .D(Lc_0), .Q(IDLE_4_q), .reset(RST));  // open: Qn, preset, en
  or or_4 (Lc, Lc_0, Write_ASCII);
  or or_5 (Ln, Ln_0, Lc_0);
  Demultiplexer #(.enable("false")) demultiplexer_3 (
    .out0(demultiplexer_3_out0), .out1(demultiplexer_3_out1), .in(IDLE_4_q), .sel(_0_n));
  D_Flip_Flop IDLE_5 (.clk(CLK), .D(demultiplexer_2_out0), .Q(\end ), .reset(RST));  // open: Qn, preset, en
  MEMORY memory_1 (
    .DIR(bit_extender_1_out), .DATA_IN(n___10___48), .WRITE(Lc_0), .CLK(CLK), .CLR(RST),
    .DATA_OUT(memory_1_data_out));
  Bit_Extender #(.in_width(32), .out_width(7)) bit_extender_2 (.in(memory_1_data_out), .out(ASCII));

  // Other names for the same wires on the sheet: Lc_1 = Write_ASCII; Sc = Write_ASCII; Ln_1 = Lc_0; Sn = Lc_0;
  //   Write = Lc_0
endmodule

module PRINT_DEC (
  input  [31:0] num,
  input  start,
  input  CLK,
  input  RST,
  output [6:0] ASCII,
  output Write_ASCII,
  output END
);

  wire demultiplexer_1_out0, demultiplexer_1_out1, demultiplexer_2_out0, demultiplexer_3_out0, end_t,
       IDLE_3_q, IDLE_q, or_1_out, or_2_out, or_3_out, S_ASCII, startUDEC, Write_ASCII_1;
  wire [6:0] ASCII_t;
  wire [31:0] multiplexer_1_out, negator_1_out;

  or or_1 (or_1_out, demultiplexer_1_out0, END);
  Negator #(.width(32)) negator_1 (.in(num), .out(negator_1_out));
  D_Flip_Flop IDLE (.clk(CLK), .D(or_1_out), .Q(IDLE_q), .preset(RST));  // open: Qn, en, reset
  Demultiplexer #(.enable("false")) demultiplexer_1 (
    .out0(demultiplexer_1_out0), .out1(demultiplexer_1_out1), .in(IDLE_q), .sel(start));
  Multiplexer #(.width(32), .enable("false")) multiplexer_1 (
    .in0(num), .in1(negator_1_out), .out(multiplexer_1_out), .sel(num[31]));
  Demultiplexer #(.enable("false")) demultiplexer_2 (
    .out0(demultiplexer_2_out0), .out1(S_ASCII), .in(demultiplexer_1_out1), .sel(num[31]));
  or or_2 (or_2_out, demultiplexer_2_out0, S_ASCII);
  D_Flip_Flop IDLE_2 (.clk(CLK), .D(or_2_out), .Q(startUDEC), .reset(RST));  // open: Qn, preset, en
  PRINT_UDEC print_udec_1 (
    .num(multiplexer_1_out), .start(startUDEC), .CLK(CLK), .RST(RST), .ASCII(ASCII_t),
    .Write_ASCII(Write_ASCII_1), .\end (end_t));
  D_Flip_Flop IDLE_3 (.clk(CLK), .D(or_3_out), .Q(IDLE_3_q), .reset(RST));  // open: Qn, preset, en
  or or_3 (or_3_out, startUDEC, demultiplexer_3_out0);
  Demultiplexer #(.enable("false")) demultiplexer_3 (
    .out0(demultiplexer_3_out0), .out1(END), .in(IDLE_3_q), .sel(end_t));
  Multiplexer #(.width(7), .enable("false")) multiplexer_2 (
    .in0(ASCII_t), .in1(7'b0101101), .out(ASCII), .sel(S_ASCII));
  or or_4 (Write_ASCII, S_ASCII, Write_ASCII_1);

  // Other names for the same wires on the sheet: sign = num[31]; Write_ASCII_0 = S_ASCII
endmodule

module TEST_PRINT (
  input  [31:0] in_1,
  output out_2
);

  wire button_1_out, button_2_out, CLK, CLR, d_ff_1_q, Write_ASCII;
  wire [6:0] ASCII;

  Button button_1 (.out(button_1_out));
  Clock clock_1 (.out(CLK));
  D_Flip_Flop d_ff_1 (.clk(CLK), .D(1'b1), .Q(d_ff_1_q), .reset(button_1_out));  // open: Qn, preset, en
  D_Flip_Flop d_ff_2 (.clk(CLK), .D(d_ff_1_q), .Qn(CLR), .reset(button_1_out));  // open: Q, preset, en
  Button button_2 (.out(button_2_out));
  PRINT_UDEC print_udec_1 ();  // open: num, start, CLK, RST, ASCII, Write_ASCII, end
  PRINT_DEC print_dec_1 (
    .num(in_1), .start(button_2_out), .CLK(CLK), .RST(CLR), .ASCII(ASCII), .Write_ASCII(Write_ASCII),
    .END(out_2));
  TTY #(.rows(32), .cols(60)) tty_1 (.data(ASCII), .clk(CLK), .we(Write_ASCII), .clr(CLR));
endmodule

module SubASM (
  input  [31:0] elemento,
  input  start,
  input  reloj,
  input  in_4,
  output [31:0] resultado,
  output \end 
);

  wire A____B, control_unit_1_lc, control_unit_1_le, control_unit_1_ln, control_unit_1_lr, control_unit_1_ls,
       not_1_out;

  Control_Unit control_unit_1 (
    .A____B(A____B), .start(start), .Reloj(reloj), .Ln(control_unit_1_ln), .Le(control_unit_1_le),
    .Lc(control_unit_1_lc), .Ls(control_unit_1_ls), .Lr(control_unit_1_lr), .\end (\end ));
  not not_1 (not_1_out, control_unit_1_ln);
  Data_Path data_path_1 (
    .Ln(not_1_out), .Lc(control_unit_1_lc), .Ls(control_unit_1_ls), .Le(control_unit_1_le),
    .Lr(control_unit_1_lr), .in_7(in_4), .Reloj(reloj), .\tamaño_de_la_lista (elemento), .A____B(A____B),
    .result(resultado));
endmodule

module Data_Path (
  input  [31:0] \tamaño_de_la_lista ,
  input  Ln,
  input  Lc,
  input  Ls,
  input  Le,
  input  Lr,
  input  in_7,
  input  Reloj,
  output A____B,
  output [31:0] result
);

  wire comparator_1_eq;
  wire [31:0] contador, divider_1_out, elem, new_suma, suma, tam;

  Register #(.width(32)) register_1 (.D(\tamaño_de_la_lista ), .en(Ln), .Q(tam), .clk(Reloj), .clr(in_7));
  Register #(.width(32), .trigger("falling")) register_2 (.D(new_suma), .en(Ls), .Q(suma), .clk(Reloj), .clr(in_7));
  Counter #(.width(32), .max('hffffffff)) counter_1 (
    .count(Lc), .Q(contador), .clk(Reloj), .clr(in_7));  // open: load, D, carry
  Register #(.width(32), .trigger("high")) register_3 (
    .D(\tamaño_de_la_lista ), .en(Le), .Q(elem), .clk(Reloj), .clr(in_7));
  Divider #(.width(32)) divider_1 (.a(suma), .b(tam), .out(divider_1_out));  // open: upper, rem
  Register #(.width(32)) register_4 (.D(divider_1_out), .en(Lr), .Q(result), .clk(Reloj), .clr(in_7));
  Adder #(.width(32)) adder_1 (.a(suma), .b(elem), .out(new_suma));  // open: cin, cout
  Comparator #(.width(32)) comparator_1 (.a(contador), .b(tam), .eq(comparator_1_eq));  // open: gt, lt
  not not_1 (A____B, comparator_1_eq);

  // Other names for the same wires on the sheet: clk = Reloj; CLR = in_7
endmodule

module Control_Unit (
  input  A____B,
  input  start,
  input  Reloj,
  output Lr,
  output Ln,
  output Le,
  output Ls,
  output Lc,
  output \end 
);

  wire and_1_out, d_ff_1_q, demultiplexer_1_out0, demultiplexer_1_out1, demultiplexer_3_out0,
       demultiplexer_3_out1, IDLE_qn, not_1_out, not_2_out, or_1_out, or_2_out, or_3_out;

  or or_1 (or_1_out, demultiplexer_1_out0, demultiplexer_3_out1);
  D_Flip_Flop IDLE (.clk(Reloj), .D(or_1_out), .Qn(IDLE_qn));  // open: Q, preset, en, reset
  Demultiplexer demultiplexer_1 (
    .out0(demultiplexer_1_out0), .out1(demultiplexer_1_out1), .in(IDLE_qn), .sel(start));  // open: en
  not not_1 (not_1_out, \end );
  and and_1 (and_1_out, demultiplexer_1_out1, not_1_out);
  or or_2 (or_2_out, and_1_out, Lc);
  Demultiplexer demultiplexer_2 (.out0(Lr), .out1(Lc), .in(d_ff_1_q), .sel(A____B));  // open: en
  D_Flip_Flop d_ff_1 (.clk(Reloj), .D(or_2_out), .Q(d_ff_1_q), .reset(\end ));  // open: Qn, preset, en
  or or_3 (or_3_out, demultiplexer_3_out0, Lr);
  D_Flip_Flop u_END (.clk(Reloj), .D(or_3_out), .Q(\end ), .reset(not_2_out));  // open: Qn, preset, en
  not not_2 (not_2_out, start);
  Demultiplexer demultiplexer_3 (
    .out0(demultiplexer_3_out0), .out1(demultiplexer_3_out1), .in(\end ), .sel(not_2_out));  // open: en

  assign Le = Lc;
  assign Ln = start;
  assign Ls = Lc;

  // Other names for the same wires on the sheet: clk = Reloj
endmodule
